# Fritzing sketch HnH17_SesorNode (saved by Fritzing 0.9.3b)
breadboards: 2

parts:
  Bauteil1 = Adafruit Feather M0 RFM9x LoRa [part_number="Adafruit #3178 or #3179"]
  Bauteil2 = VERTER 5V USB Buck-Boost

nets:
  N1: Bauteil1.DIO1, Bauteil1.D6
  GND: Bauteil1.GND, Bauteil2.GND
  +3V3: Bauteil1.+3V3, Bauteil2.VIN

custom parts:
  Adafruit Feather M0 RFM9x LoRa: This is the Adafruit Feather M0 RFM95 LoRa Radio - our take on an microcontroller with a "Long Range (LoRa)" packet radio transceiver with built in USB and battery charging. Its an Adafruit Feather M0 with a 433Mhz or 900MHz radio module cooked in! Great for making wireless networks that are more flexible than Bluetooth LE and without the high power requirements of WiFi. We have other boards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
  VERTER 5V USB Buck-Boost: VERTER can take battery voltages from 3-12VDC and output a nice 5V DC, which makes it a perfect universal power supply for your portable project! Where Verter really shines is when you have a battery or power range that can fluctuate a lot, or you don't know what you'll end up using.
